# Fritzing sketch fritzing projet (saved by Fritzing 0.9.3b)
breadboards: 1

parts:
  Composant1 = Arduino Uno (Rev3)
  R1 = Resistor [tolerance=±5% resistance=10k package=THT]
  L1 = Inductor [inductance=10mH package="400 mil [THT]"]
  D1 = Rectifier Diode [part_number=1N4001 package="300 mil [THT]"]
  C2 = Ceramic Capacitor [capacitance=10nF package="100 mil [THT, multilayer]"]
  R2 = Resistor [tolerance=±5% resistance=1M package=THT]
  R3 = Resistor [tolerance=±5% resistance=3.3k package=THT]  # not connected
  C1 = Ceramic Capacitor [capacitance=0.1nF package="100 mil [THT, multilayer]"]  # not connected
  LED1 = LED - 5mm [color="Red (633nm)" package="5 mm [THT]"]
  LED2 = LED - 5mm [color="Red (633nm)" package="5 mm [THT]"]
  LED3 = LED - 5mm [color="Red (633nm)" package="5 mm [THT]"]
  R4 = Resistor [tolerance=±5% resistance=220 package=THT]

nets:
  N1: Composant1.D9_PWM, R1.Pin_1
  N2: Composant1.GND, R2.Pin_0, R4.Pin_1
  N3: Composant1.D2, LED1.anode
  N4: Composant1.D3_PWM, LED2.anode
  N5: Composant1.D4, LED3.anode
  N6: R1.Pin_0, L1.pin_1
  N7: L1.pin_0, D1.anode, C2.0
  N8: D1.cathode, R2.Pin_1
  N9: LED1.cathode, LED2.cathode, LED3.cathode, R4.Pin_0
